// Logisim project CPU.circ as structural Verilog: 10 circuits, main circuit main
module main (
  input  in_1,
  output RegWrite,
  output MemWrite,
  output [31:0] Instr,
  output [4:0] RegAddr,
  output [31:0] MemAddr,
  output [31:0] pc,
  output [31:0] RegData,
  output [31:0] MemData
);

  wire aluSrc, aluZero, and_1_out, branch, clk, extendType, if_byte, if_half, jump, jumpSrc, regDst, regPc,
       regRa, regSrc, shiftSrc;
  wire [3:0] aluControl;
  wire [4:0] bit_extender_3_out, multiplexer_1_out, shift;
  wire [31:0] bit_extender_1_out, bit_extender_2_out, dm_1_rd, extend, multiplexer_4_out, multiplexer_6_out,
       PC_4, PC_next, rd1;

  Clock clock_1 (.out(clk));
  and and_1 (and_1_out, aluZero, branch);
  IFU ifu_1 (.RD(Instr), .PC(pc), .NEXT_PC(PC_next), .clk(clk), .reset(in_1));
  NPC npc_1 (
    .PC(pc), .imm({Instr[20:16], Instr[25:21], Instr[15:0]}), .offest(Instr[15:0]), .if_branch(and_1_out),
    .if_jump(jump), .PC_next(PC_next), .rs(rd1), .jumpSrc(jumpSrc), .out_9(PC_4));
  Multiplexer #(.width(5)) multiplexer_1 (
    .in0(Instr[20:16]), .in1(Instr[15:11]), .out(multiplexer_1_out), .sel(regDst), .en(1'b1));
  controlUnit controlunit_1 (
    .out_4(regDst), .out_3(RegWrite), .out_10(branch), .out_6(aluSrc), .out_11(aluControl), .out_9(MemWrite),
    .op(Instr[31:26]), .func(Instr[5:0]), .out_5(regSrc), .out_7(extendType), .out_8(shiftSrc),
    .out_12(regRa), .out_13(regPc), .out_14(jumpSrc), .out_15(jump), .if_byte(if_byte), .if_half(if_half));
  Multiplexer #(.width(5)) multiplexer_2 (
    .in0(multiplexer_1_out), .in1({5{1'b1}}), .out(RegAddr), .sel(regRa), .en(1'b1));
  assign bit_extender_1_out = {{16{Instr[15]}}, Instr[15:0]};  // Bit_Extender bit_extender_1
  assign bit_extender_2_out = {{16{1'b0}}, Instr[15:0]};  // Bit_Extender bit_extender_2
  Multiplexer #(.width(32)) multiplexer_3 (
    .in0(bit_extender_1_out), .in1(bit_extender_2_out), .out(extend), .sel(extendType), .en(1'b1));
  GRF grf_1 (
    .clk(clk), .reset(in_1), .WE(RegWrite), .A1(Instr[25:21]), .A2(Instr[20:16]), .A3(RegAddr), .WD(RegData),
    .RD1(rd1), .RD2(MemData));
  Multiplexer #(.width(32)) multiplexer_4 (
    .in0(MemData), .in1(extend), .out(multiplexer_4_out), .sel(aluSrc), .en(1'b1));
  Bit_Extender #(.in_width(32), .out_width(5)) bit_extender_3 (.in(rd1), .out(bit_extender_3_out));
  ALU alu_1 (.srcA(rd1), .srcB(multiplexer_4_out), .op(aluControl), .shift(shift), .result(MemAddr), .zero(aluZero));
  Multiplexer #(.width(5)) multiplexer_5 (
    .in0(bit_extender_3_out), .in1(Instr[10:6]), .out(shift), .sel(shiftSrc), .en(1'b1));
  DM dm_1 (
    .address(MemAddr), .data(MemData), .WE(MemWrite), .clk(clk), .RD(dm_1_rd), .if_byte(if_byte),
    .if_half(if_half));
  Multiplexer #(.width(32)) multiplexer_6 (
    .in0(MemAddr), .in1(dm_1_rd), .out(multiplexer_6_out), .sel(regSrc), .en(1'b1));
  Multiplexer #(.width(32)) multiplexer_7 (.in0(multiplexer_6_out), .in1(PC_4), .out(RegData), .sel(regPc), .en(1'b1));

  // Other names for the same wires on the sheet: aluResult[31:0] = MemAddr; func[5:0] = Instr[5:0];
  //   imm[25:0] = {Instr[20:16], Instr[25:21], Instr[15:0]}; offest[15:0] = Instr[15:0]; shamt[4:0] = Instr[10:6];
  //   rd[4:0] = Instr[15:11]; rs[4:0] = Instr[25:21]; rt[4:0] = Instr[20:16]; op[5:0] = Instr[31:26];
  //   rd2[31:0] = MemData; reset = in_1
endmodule

module GRF (
  input  clk,
  input  reset,
  input  WE,
  input  [4:0] A1,
  input  [4:0] A2,
  input  [4:0] A3,
  input  [31:0] WD,
  output [31:0] RD1,
  output [31:0] RD2
);

  wire WE0, WE1, WE2, WE3, WE4, WE5, WE6, WE7, WE8, WE9, WE10, WE11, WE12, WE13, WE14, WE15, WE16, WE17,
       WE18, WE19, WE20, WE21, WE22, WE23, WE24, WE25, WE26, WE27, WE28, WE29, WE30, WE31;
  wire [31:0] O1, O2, O3, O4, O5, O6, O7, O8, O9, O10, O11, O12, O13, O14, O15, O16, O17, O18, O19, O20, O21,
       O22, O23, O24, O25, O26, O27, O28, O29, O30, O31;

  Register #(.width(32)) R0 (.en(WE0), .clk(clk), .clr(reset));  // open: D, Q
  Register #(.width(32)) R8 (.D(WD), .en(WE8), .Q(O8), .clk(clk), .clr(reset));
  Register #(.width(32)) R16 (.D(WD), .en(WE16), .Q(O16), .clk(clk), .clr(reset));
  Register #(.width(32)) R24 (.D(WD), .en(WE24), .Q(O24), .clk(clk), .clr(reset));
  Multiplexer #(.select(5), .width(32)) multiplexer_1 (
    .in0({32{1'b0}}), .in1(O1), .in2(O2), .in3(O3), .in4(O4), .in5(O5), .in6(O6), .in7(O7), .in8(O8),
    .in9(O9), .in10(O10), .in11(O11), .in12(O12), .in13(O13), .in14(O14), .in15(O15), .in16(O16), .in17(O17),
    .in18(O18), .in19(O19), .in20(O20), .in21(O21), .in22(O22), .in23(O23), .in24(O24), .in25(O25),
    .in26(O26), .in27(O27), .in28(O28), .in29(O29), .in30(O30), .in31(O31), .out(RD1), .sel(A1), .en(1'b1));
  Register #(.width(32)) R1 (.D(WD), .en(WE1), .Q(O1), .clk(clk), .clr(reset));
  Register #(.width(32)) R9 (.D(WD), .en(WE9), .Q(O9), .clk(clk), .clr(reset));
  Register #(.width(32)) R17 (.D(WD), .en(WE17), .Q(O17), .clk(clk), .clr(reset));
  Register #(.width(32)) R25 (.D(WD), .en(WE25), .Q(O25), .clk(clk), .clr(reset));
  Register #(.width(32)) R2 (.D(WD), .en(WE2), .Q(O2), .clk(clk), .clr(reset));
  Register #(.width(32)) R10 (.D(WD), .en(WE10), .Q(O10), .clk(clk), .clr(reset));
  Register #(.width(32)) R18 (.D(WD), .en(WE18), .Q(O18), .clk(clk), .clr(reset));
  Register #(.width(32)) R26 (.D(WD), .en(WE26), .Q(O26), .clk(clk), .clr(reset));
  Multiplexer #(.select(5), .width(32)) multiplexer_2 (
    .in0({32{1'b0}}), .in1(O1), .in2(O2), .in3(O3), .in4(O4), .in5(O5), .in6(O6), .in7(O7), .in8(O8),
    .in9(O9), .in10(O10), .in11(O11), .in12(O12), .in13(O13), .in14(O14), .in15(O15), .in16(O16), .in17(O17),
    .in18(O18), .in19(O19), .in20(O20), .in21(O21), .in22(O22), .in23(O23), .in24(O24), .in25(O25),
    .in26(O26), .in27(O27), .in28(O28), .in29(O29), .in30(O30), .in31(O31), .out(RD2), .sel(A2), .en(1'b1));
  Register #(.width(32)) R3 (.D(WD), .en(WE3), .Q(O3), .clk(clk), .clr(reset));
  Register #(.width(32)) R11 (.D(WD), .en(WE11), .Q(O11), .clk(clk), .clr(reset));
  Register #(.width(32)) R19 (.D(WD), .en(WE19), .Q(O19), .clk(clk), .clr(reset));
  Register #(.width(32)) R27 (.D(WD), .en(WE27), .Q(O27), .clk(clk), .clr(reset));
  Demultiplexer #(.select(5)) demultiplexer_1 (
    .out0(WE0), .out1(WE1), .out2(WE2), .out3(WE3), .out4(WE4), .out5(WE5), .out6(WE6), .out7(WE7),
    .out8(WE8), .out9(WE9), .out10(WE10), .out11(WE11), .out12(WE12), .out13(WE13), .out14(WE14),
    .out15(WE15), .out16(WE16), .out17(WE17), .out18(WE18), .out19(WE19), .out20(WE20), .out21(WE21),
    .out22(WE22), .out23(WE23), .out24(WE24), .out25(WE25), .out26(WE26), .out27(WE27), .out28(WE28),
    .out29(WE29), .out30(WE30), .out31(WE31), .in(WE), .sel(A3), .en(1'b1));
  Register #(.width(32)) R4 (.D(WD), .en(WE4), .Q(O4), .clk(clk), .clr(reset));
  Register #(.width(32)) R12 (.D(WD), .en(WE12), .Q(O12), .clk(clk), .clr(reset));
  Register #(.width(32)) R20 (.D(WD), .en(WE20), .Q(O20), .clk(clk), .clr(reset));
  Register #(.width(32)) R28 (.D(WD), .en(WE28), .Q(O28), .clk(clk), .clr(reset));
  Register #(.width(32)) R5 (.D(WD), .en(WE5), .Q(O5), .clk(clk), .clr(reset));
  Register #(.width(32)) R13 (.D(WD), .en(WE13), .Q(O13), .clk(clk), .clr(reset));
  Register #(.width(32)) R21 (.D(WD), .en(WE21), .Q(O21), .clk(clk), .clr(reset));
  Register #(.width(32)) R29 (.D(WD), .en(WE29), .Q(O29), .clk(clk), .clr(reset));
  Register #(.width(32)) R6 (.D(WD), .en(WE6), .Q(O6), .clk(clk), .clr(reset));
  Register #(.width(32)) R14 (.D(WD), .en(WE14), .Q(O14), .clk(clk), .clr(reset));
  Register #(.width(32)) R22 (.D(WD), .en(WE22), .Q(O22), .clk(clk), .clr(reset));
  Register #(.width(32)) R30 (.D(WD), .en(WE30), .Q(O30), .clk(clk), .clr(reset));
  Register #(.width(32)) R7 (.D(WD), .en(WE7), .Q(O7), .clk(clk), .clr(reset));
  Register #(.width(32)) R15 (.D(WD), .en(WE15), .Q(O15), .clk(clk), .clr(reset));
  Register #(.width(32)) R23 (.D(WD), .en(WE23), .Q(O23), .clk(clk), .clr(reset));
  Register #(.width(32)) R31 (.D(WD), .en(WE31), .Q(O31), .clk(clk), .clr(reset));
endmodule

module ALU (
  input  [31:0] srcA,
  input  [31:0] srcB,
  input  [3:0] op,
  input  [4:0] shift,
  output [31:0] result,
  output zero
);

  wire comparator_1_lt;
  wire [31:0] A___B, A___B_t, A___B_t_t, A___B_t_t_t, A___B_t_t_t_t, A_xor_B, B____16, B_____shift,
       B____shift, B____shift_t, n_A___B, or_2_out;

  assign A___B = srcA & srcB;  // AND_Gate and_1, 32 bits wide
  Adder #(.width(32)) adder_1 (.a(srcA), .b(srcB), .out(A___B_t));  // open: cin, cout
  Shifter #(.width(32)) shifter_1 (.in(srcB), .\dist (shift), .out(B____shift));
  Comparator #(.width(32)) comparator_1 (.a(srcA), .b(srcB), .lt(comparator_1_lt));  // open: gt, eq
  assign A___B_t_t_t = {{31{1'b0}}, comparator_1_lt};  // Bit_Extender bit_extender_1
  assign A___B_t_t_t_t = srcA | srcB;  // OR_Gate or_1, 32 bits wide
  Subtractor #(.width(32)) subtractor_1 (.a(srcA), .b(srcB), .out(A___B_t_t));  // open: bin, bout
  Shifter #(.width(32), .shift("lr")) shifter_2 (.in(srcB), .\dist (shift), .out(B____shift_t));
  assign A_xor_B = srcA ^ srcB;  // XOR_Gate xor_1, 32 bits wide
  Shifter #(.width(32), .shift("ar")) shifter_3 (.in(srcB), .\dist (shift), .out(B_____shift));
  Multiplexer #(.select(4), .width(32)) multiplexer_1 (
    .in0(A___B_t), .in1(A___B_t_t), .in2(A___B), .in3(A___B_t_t_t_t), .in4(A_xor_B), .in5(n_A___B),
    .in6(B____shift), .in7(B____shift_t), .in8(B_____shift), .in9(B____16), .in10(A___B_t_t_t), .out(result),
    .sel(op), .en(1'b1));  // open: in11, in12, in13, in14, in15
  assign or_2_out = srcA | srcB;  // OR_Gate or_2, 32 bits wide
  Shifter #(.width(32)) shifter_4 (.in(srcB), .\dist (5'b10000), .out(B____16));
  Comparator #(.width(32)) comparator_2 (.a(result), .b({32{1'b0}}), .eq(zero));  // open: gt, lt
  assign n_A___B = ~or_2_out;  // NOT_Gate not_1, 32 bits wide
endmodule

module IFU (
  input  [31:0] NEXT_PC,
  input  clk,
  input  reset,
  output [31:0] PC,
  output [31:0] RD
);

  wire comparator_1_eq;
  wire [11:0] bit_extender_1_out;
  wire [31:0] register_1_q, shifter_1_out, subtractor_1_out;

  Register #(.width(32)) register_1 (.D(NEXT_PC), .Q(register_1_q), .clk(clk), .clr(reset));  // open: en
  Comparator #(.width(32)) comparator_1 (.a({32{1'b0}}), .b(register_1_q), .eq(comparator_1_eq));  // open: gt, lt
  Multiplexer #(.width(32)) multiplexer_1 (
    .in0(register_1_q), .in1(32'h3000), .out(PC), .sel(comparator_1_eq), .en(1'b1));
  Subtractor #(.width(32)) subtractor_1 (.a(PC), .b(32'h3000), .out(subtractor_1_out));  // open: bin, bout
  Shifter #(.width(32), .shift("lr")) shifter_1 (.in(subtractor_1_out), .\dist (5'b00010), .out(shifter_1_out));
  Bit_Extender #(.in_width(32), .out_width(12)) bit_extender_1 (.in(shifter_1_out), .out(bit_extender_1_out));
  ROM #(.addrWidth(12), .dataWidth(32)) rom_1 (.addr(bit_extender_1_out), .data(RD));  // open: sel

  // Notes on the sheet:
  //   contents of rom_1 (hex, n*v repeats v):
  //   3c011234 34215678 ac010000 8c070000 80010000 80020001 80030002 80040003 a0010003 a0020002 a0030001
  //   a0040000 8c050000
endmodule

module DM (
  input  [31:0] address,
  input  [31:0] data,
  input  WE,
  input  clk,
  input  if_byte,
  input  if_half,
  output [31:0] RD
);

  wire [4:0] bit_extender_5_out, bit_extender_7_out, shift, shift2;
  wire [23:0] address_t;
  wire [31:0] and_1_out, and_2_out, bit_extender_1_out, bit_extender_2_out, bit_extender_4_out,
       bit_extender_6_out, dm, multiplexer_1_out, multiplexer_2_out, not_1_out, not_2_out, or_1_out,
       or_2_out, shifter_1_out, shifter_2_out, shifter_3_out, shifter_4_out, shifter_5_out, shifter_7_out,
       shifter_8_out, WD;

  Shifter #(.width(32), .shift("lr")) shifter_1 (.in(dm), .\dist (shift), .out(shifter_1_out));
  assign bit_extender_1_out = {{24{1'b0}}, data[7:0]};  // Bit_Extender bit_extender_1
  Shifter #(.width(32)) shifter_2 (.in(32'hff), .\dist (shift), .out(shifter_2_out));
  assign bit_extender_2_out = {{24{1'b0}}, shifter_1_out[7:0]};  // Bit_Extender bit_extender_2
  Shifter #(.width(32), .shift("lr")) shifter_3 (.in(address), .\dist (5'b00010), .out(shifter_3_out));
  Shifter #(.width(32)) shifter_4 (.in(bit_extender_1_out), .\dist (shift), .out(shifter_4_out));
  assign not_1_out = ~shifter_2_out;  // NOT_Gate not_1, 32 bits wide
  assign and_1_out = not_1_out & dm;  // AND_Gate and_1, 32 bits wide
  Multiplexer #(.width(32)) multiplexer_1 (
    .in0(dm), .in1(bit_extender_2_out), .out(multiplexer_1_out), .sel(if_byte), .en(1'b1));
  Bit_Extender #(.in_width(32), .out_width(24)) bit_extender_3 (.in(shifter_3_out), .out(address_t));
  assign or_1_out = shifter_4_out | and_1_out;  // OR_Gate or_1, 32 bits wide
  Shifter #(.width(32), .shift("lr")) shifter_5 (.in(dm), .\dist (shift2), .out(shifter_5_out));
  Multiplexer #(.width(32)) multiplexer_2 (
    .in0(data), .in1(or_1_out), .out(multiplexer_2_out), .sel(if_byte), .en(1'b1));
  assign bit_extender_4_out = {{16{1'b0}}, shifter_5_out[15:0]};  // Bit_Extender bit_extender_4
  assign bit_extender_5_out = {{3{1'b0}}, address[1:0]};  // Bit_Extender bit_extender_5
  assign bit_extender_6_out = {{16{1'b0}}, data[15:0]};  // Bit_Extender bit_extender_6
  Multiplexer #(.width(32)) multiplexer_3 (
    .in0(multiplexer_1_out), .in1(bit_extender_4_out), .out(RD), .sel(if_half), .en(1'b1));
  Shifter #(.width(5)) shifter_6 (.in(bit_extender_5_out), .\dist (3'b011), .out(shift));
  Shifter #(.width(32)) shifter_7 (.in(bit_extender_6_out), .\dist (shift2), .out(shifter_7_out));
  Shifter #(.width(32)) shifter_8 (.in(32'hff), .\dist (shift2), .out(shifter_8_out));
  assign not_2_out = ~shifter_8_out;  // NOT_Gate not_2, 32 bits wide
  assign and_2_out = not_2_out & dm;  // AND_Gate and_2, 32 bits wide
  assign or_2_out = shifter_7_out | and_2_out;  // OR_Gate or_2, 32 bits wide
  assign bit_extender_7_out = {{4{1'b0}}, address[1]};  // Bit_Extender bit_extender_7
  RAM #(.addrWidth(24), .dataWidth(32), .bus("separate")) ram_1 (
    .addr(address_t), .din(WD), .data(dm), .str(WE), .clk(clk));  // open: sel, ld, clr
  Multiplexer #(.width(32)) multiplexer_4 (.in0(multiplexer_2_out), .in1(or_2_out), .out(WD), .sel(if_half), .en(1'b1));
  Shifter #(.width(5)) shifter_9 (.in(bit_extender_7_out), .\dist (3'b100), .out(shift2));

  // Other names for the same wires on the sheet: byte[1:0] = address[1:0]; half = address[1]
endmodule

module controlUnit (
  input  [5:0] op,
  input  [5:0] func,
  output out_3,
  output out_4,
  output out_5,
  output out_6,
  output out_7,
  output out_8,
  output out_9,
  output out_10,
  output [3:0] out_11,
  output out_12,
  output out_13,
  output out_14,
  output out_15,
  output if_byte,
  output if_half
);

  wire and_1_out, comparator_1_eq, comparator_2_eq, comparator_3_eq, comparator_4_eq, comparator_5_eq,
       comparator_6_eq, comparator_7_eq, or_3_out, regWrite;
  wire [2:0] control1_aluop;

  // Probe on control1_aluop
  JumpControl jumpcontrol_1 (.op(op), .func(func), .regRa(out_12), .regPc(out_13), .jumpSrc(out_14), .jump(out_15));
  control1 control1 (
    .op(op), .aluOp(control1_aluop), .regWrite(regWrite), .regDst(out_4), .regSrc(out_5), .aluSrc(out_6),
    .extendType(out_7), .memWwrite(out_9), .branch(out_10));
  control2 control2 (.func(func), .aluControl(out_11), .aluOp(control1_aluop), .shiftSrc(out_8));
  Comparator #(.width(6)) comparator_1 (.a(op), .b(6'b101000), .eq(comparator_1_eq));  // open: gt, lt
  Comparator #(.width(6)) comparator_2 (.a(op), .b(6'b100000), .eq(comparator_2_eq));  // open: gt, lt
  Comparator #(.width(6)) comparator_3 (.a(op), .b(6'b101001), .eq(comparator_3_eq));  // open: gt, lt
  Comparator #(.width(6)) comparator_4 (.a(op), .b(6'b100001), .eq(comparator_4_eq));  // open: gt, lt
  Comparator #(.width(6)) comparator_5 (.a(op), .b(6'b000011), .eq(comparator_5_eq));  // open: gt, lt
  Comparator #(.width(6)) comparator_6 (.a(func), .b(6'b001001), .eq(comparator_6_eq));  // open: gt, lt
  and and_1 (and_1_out, comparator_6_eq, comparator_7_eq);
  Comparator #(.width(6)) comparator_7 (.a(op), .b({6{1'b0}}), .eq(comparator_7_eq));  // open: gt, lt
  or or_1 (if_byte, comparator_1_eq, comparator_2_eq);
  or or_2 (if_half, comparator_3_eq, comparator_4_eq);
  or or_3 (or_3_out, comparator_5_eq, and_1_out);
  or or_4 (out_3, regWrite, or_3_out);

  // Other names for the same wires on the sheet: aluControl[3:0] = out_11; aluSrc = out_6; branch = out_10;
  //   extendType = out_7; jump = out_15; jumpSrc = out_14; memWrite = out_9; regDst = out_4; regPc = out_13;
  //   regRa = out_12; regSrc = out_5; shiftSrc = out_8
endmodule

module control1 (
  input  [5:0] op,
  output [2:0] aluOp,
  output regWrite,
  output regDst,
  output regSrc,
  output aluSrc,
  output extendType,
  output memWwrite,
  output branch
);

  wire and_1_out, and_2_out, and_3_out, and_10_out, not_1_out, not_2_out, not_3_out, not_4_out, not_5_out,
       not_6_out, not_7_out, not_8_out, not_9_out, not_10_out, not_11_out, not_12_out, not_13_out, not_14_out;

  not not_1 (not_1_out, op[3]);
  not not_2 (not_2_out, op[2]);
  not not_3 (not_3_out, op[1]);
  not not_4 (not_4_out, op[5]);
  not not_5 (not_5_out, op[3]);
  not not_6 (not_6_out, op[5]);
  not not_7 (not_7_out, op[3]);
  or or_1 (aluSrc, op[0], op[5]);
  not not_8 (not_8_out, op[5]);
  not not_9 (not_9_out, op[1]);
  not not_10 (not_10_out, op[2]);
  not not_11 (not_11_out, op[3]);
  not not_12 (not_12_out, op[5]);
  not not_13 (not_13_out, op[1]);
  not not_14 (not_14_out, op[1]);
  and and_1 (and_1_out, not_1_out, not_2_out, not_3_out);
  and and_2 (and_2_out, not_4_out, op[0]);
  and and_3 (and_3_out, op[5], not_5_out);
  and and_4 (regDst, not_6_out, not_7_out);
  and and_5 (extendType, not_8_out, op[3], not_9_out);
  and and_6 (memWwrite, op[3], not_10_out);
  and and_7 (branch, not_11_out, op[2]);
  and and_8 (aluOp[2], not_12_out, op[1]);
  and and_9 (aluOp[1], op[2], not_13_out);
  and and_10 (and_10_out, op[3], not_14_out);
  or or_2 (regWrite, and_1_out, and_2_out, and_3_out);
  or or_3 (aluOp[0], and_10_out, op[5]);

  assign regSrc = op[5];
endmodule

module control2 (
  input  [5:0] func,
  input  [2:0] aluOp,
  output [3:0] aluControl,
  output shiftSrc
);

  wire aluControl0, aluControl00, aluControl1, aluControl11, aluControl22, and_1_out, and_2_out,
       comparator_1_eq, comparator_2_eq, not_2_out, not_3_out, not_4_out, not_5_out, not_6_out, shiftSrc_t;

  not not_1 (aluControl22, func[5]);
  not not_2 (not_2_out, func[5]);
  not not_3 (not_3_out, func[3]);
  not not_4 (not_4_out, func[5]);
  not not_5 (not_5_out, func[2]);
  or or_1 (aluControl11, not_2_out, func[2], func[3]);
  and and_1 (and_1_out, not_3_out, func[1]);
  and and_2 (and_2_out, func[5], func[2]);
  and and_3 (shiftSrc_t, not_4_out, not_5_out);
  or or_2 (aluControl00, and_1_out, and_2_out);
  Comparator #(.width(3)) comparator_1 (.a(aluOp), .b(3'b000), .eq(comparator_1_eq));  // open: gt, lt
  and and_4 (aluControl1, aluOp[1], aluOp[0]);
  not not_6 (not_6_out, aluOp[0]);
  or or_3 (aluControl0, not_6_out, aluOp[1]);
  Multiplexer #(.width(4)) multiplexer_1 (
    .in0({aluOp[2], 1'b0, aluControl1, aluControl0}),
    .in1({func[3], aluControl22, aluControl11, aluControl00}), .out(aluControl), .sel(comparator_1_eq),
    .en(1'b1));
  Comparator #(.width(3)) comparator_2 (.a(aluOp), .b(3'b000), .eq(comparator_2_eq));  // open: gt, lt
  Multiplexer multiplexer_2 (.in0(1'b0), .in1(shiftSrc_t), .out(shiftSrc), .sel(comparator_2_eq), .en(1'b1));

  // Other names for the same wires on the sheet: aluout0 = aluOp[0]; aluout1 = aluOp[1];
  //   control0 (some bits) = {aluOp[2], aluControl1, aluControl0}; aluControl3 = aluOp[2]; aluout2 = aluOp[2];
  //   control1[3:0] = {func[3], aluControl22, aluControl11, aluControl00}; aluControl33 = func[3]
endmodule

module NPC (
  input  [31:0] PC,
  input  [25:0] imm,
  input  [15:0] offest,
  input  if_branch,
  input  if_jump,
  input  jumpSrc,
  input  [31:0] rs,
  output [31:0] PC_next,
  output [31:0] out_9
);

  wire [15:0] shifter_1_out;
  wire [27:0] bit_extender_1_out, shifter_2_out;
  wire [31:0] bit_extender_2_out, multiplexer_1_out, PC_branch, PC_jump;

  Multiplexer #(.width(32)) multiplexer_1 (
    .in0(out_9), .in1(PC_branch), .out(multiplexer_1_out), .sel(if_branch), .en(1'b1));
  Multiplexer #(.width(32)) multiplexer_2 (
    .in0(multiplexer_1_out), .in1(PC_jump), .out(PC_next), .sel(if_jump), .en(1'b1));
  Shifter #(.width(16)) shifter_1 (.in(offest), .\dist (4'b0010), .out(shifter_1_out));
  assign bit_extender_1_out = {{2{1'b0}}, imm};  // Bit_Extender bit_extender_1
  Shifter #(.width(28)) shifter_2 (.in(bit_extender_1_out), .\dist (5'b00010), .out(shifter_2_out));
  assign bit_extender_2_out = {{16{shifter_1_out[15]}}, shifter_1_out};  // Bit_Extender bit_extender_2
  Adder #(.width(32)) adder_1 (.a(PC), .b(32'h4), .out(out_9));  // open: cin, cout
  Adder #(.width(32)) adder_2 (.a(out_9), .b(bit_extender_2_out), .out(PC_branch));  // open: cin, cout
  Multiplexer #(.width(32)) multiplexer_3 (
    .in0({PC[31:28], shifter_2_out}), .in1(rs), .out(PC_jump), .sel(jumpSrc), .en(1'b1));

  // Other names for the same wires on the sheet: PC_4[31:0] = out_9
endmodule

module JumpControl (
  input  [5:0] op,
  input  [5:0] func,
  output regRa,
  output regPc,
  output jumpSrc,
  output jump
);

  wire and_1_out, and_3_out, comparator_1_eq, comparator_2_eq, comparator_3_eq, comparator_4_eq,
       comparator_5_eq, comparator_6_eq, comparator_7_eq, comparator_8_eq, comparator_10_eq,
       comparator_11_eq, comparator_12_eq, or_1_out, or_2_out;

  Comparator #(.width(6)) comparator_1 (.a(op), .b(6'b000011), .eq(comparator_1_eq));  // open: gt, lt
  Comparator #(.width(6)) comparator_2 (.a(func), .b(6'b001001), .eq(comparator_2_eq));  // open: gt, lt
  Comparator #(.width(6)) comparator_3 (.a(op), .b({6{1'b0}}), .eq(comparator_3_eq));  // open: gt, lt
  Comparator #(.width(6)) comparator_4 (.a(func), .b(6'b001000), .eq(comparator_4_eq));  // open: gt, lt
  Comparator #(.width(6)) comparator_5 (.a(func), .b(6'b001001), .eq(comparator_5_eq));  // open: gt, lt
  Comparator #(.width(6)) comparator_6 (.a(func), .b(6'b001000), .eq(comparator_6_eq));  // open: gt, lt
  or or_1 (or_1_out, comparator_6_eq, comparator_7_eq);
  Comparator #(.width(6)) comparator_7 (.a(func), .b(6'b001001), .eq(comparator_7_eq));  // open: gt, lt
  Comparator #(.width(6)) comparator_8 (.a(op), .b({6{1'b0}}), .eq(comparator_8_eq));  // open: gt, lt
  Comparator #(.width(6)) comparator_9 (.a(op), .b(6'b000011), .eq(regRa));  // open: gt, lt
  and and_1 (and_1_out, comparator_2_eq, comparator_3_eq);
  or or_2 (or_2_out, comparator_4_eq, comparator_5_eq);
  and and_2 (jumpSrc, or_2_out, comparator_10_eq);
  Comparator #(.width(6)) comparator_10 (.a(op), .b({6{1'b0}}), .eq(comparator_10_eq));  // open: gt, lt
  Comparator #(.width(6)) comparator_11 (.a(op), .b(6'b000010), .eq(comparator_11_eq));  // open: gt, lt
  Comparator #(.width(6)) comparator_12 (.a(op), .b(6'b000011), .eq(comparator_12_eq));  // open: gt, lt
  and and_3 (and_3_out, or_1_out, comparator_8_eq);
  or or_3 (regPc, comparator_1_eq, and_1_out);
  or or_4 (jump, comparator_11_eq, comparator_12_eq, and_3_out);
endmodule
