// Logisim project 1109-22 mod5.circ as structural Verilog
module Mealy (
  input  [1:0] in_1,
  input  b,
  output [1:0] out_3
);

  wire and_1_out, and_2_out, and_3_out, and_4_out, and_5_out, and_6_out, not_1_out, not_2_out, not_3_out,
       not_4_out, not_5_out, not_6_out, not_7_out, not_8_out;

  not not_1 (not_1_out, in_1[0]);
  and and_1 (and_1_out, not_1_out, in_1[1]);
  and and_2 (and_2_out, in_1[0], not_2_out);
  not not_2 (not_2_out, in_1[1]);
  and and_3 (and_3_out, in_1[0], b);
  not not_3 (not_3_out, in_1[0]);
  and and_4 (and_4_out, not_3_out, not_4_out, b);
  not not_4 (not_4_out, in_1[1]);
  not not_5 (not_5_out, in_1[0]);
  and and_5 (and_5_out, not_5_out, in_1[1], not_6_out);
  not not_6 (not_6_out, b);
  not not_7 (not_7_out, in_1[1]);
  and and_6 (and_6_out, in_1[0], not_7_out, not_8_out);
  not not_8 (not_8_out, b);
  // Probe on out_3[0]
  or or_1 (out_3[0], and_1_out, and_2_out, and_3_out);
  or or_2 (out_3[1], and_4_out, and_5_out, and_6_out);
  // Probe on out_3[1]
endmodule

module \output  (
  input  [1:0] in_1,
  input  b,
  output D0,
  output D1,
  output D2,
  output D3,
  output D4
);

  wire and_1_out, and_2_out, and_3_out, and_4_out, and_5_out, and_6_out, and_7_out, and_8_out, not_1_out,
       not_2_out, not_3_out, not_4_out, not_5_out, not_6_out, not_7_out, not_8_out, not_9_out, not_10_out,
       not_11_out, not_12_out;

  not not_1 (not_1_out, in_1[0]);
  not not_2 (not_2_out, in_1[1]);
  not not_3 (not_3_out, b);
  not not_4 (not_4_out, b);
  not not_5 (not_5_out, in_1[0]);
  not not_6 (not_6_out, in_1[1]);
  not not_7 (not_7_out, in_1[0]);
  not not_8 (not_8_out, in_1[1]);
  not not_9 (not_9_out, in_1[0]);
  not not_10 (not_10_out, b);
  not not_11 (not_11_out, in_1[1]);
  not not_12 (not_12_out, b);
  and and_1 (and_1_out, not_1_out, not_2_out, not_3_out);
  and and_2 (and_2_out, in_1[0], in_1[1], not_4_out);
  and and_3 (and_3_out, not_5_out, not_6_out, b);
  and and_4 (and_4_out, in_1[0], in_1[1], b);
  and and_5 (and_5_out, not_7_out, in_1[1], b);
  and and_6 (and_6_out, in_1[0], not_8_out, b);
  and and_7 (and_7_out, not_9_out, in_1[1], not_10_out);
  and and_8 (and_8_out, in_1[0], not_11_out, not_12_out);
  or or_1 (D1, and_1_out, and_2_out);
  or or_2 (D2, and_3_out, and_4_out);
  or or_3 (D3, and_5_out, and_6_out);
  or or_4 (D4, and_7_out, and_8_out);

  assign D0 = 1'b0;
endmodule

module mod5 (
  input  in_1,
  output out_2,
  output out_3,
  output out_4,
  output out_5,
  output out_6
);

  wire clock_1_out;
  wire [1:0] mealy_1_out_3, register_1_q;

  // Probe on register_1_q
  Mealy mealy_1 (.in_1(register_1_q), .b(in_1), .out_3(mealy_1_out_3));
  // Probe on mealy_1_out_3
  Clock clock_1 (.out(clock_1_out));
  // Probe on register_1_q
  Register #(.width(2)) register_1 (.D(mealy_1_out_3), .Q(register_1_q), .clk(clock_1_out));  // open: en, clr
  \output  output_1 (.in_1(register_1_q), .b(in_1), .D0(out_2), .D1(out_3), .D2(out_4), .D3(out_5), .D4(out_6));
endmodule
