// Logisim project 1109-23 fibonacci-challenge.circ as structural Verilog: 5 circuits, main circuit main
module main (
  input  [31:0] N,
  output [31:0] out_2,
  output [31:0] out_3,
  output [31:0] out_4,
  output [31:0] out_5
);

  wire if_is_0, if_lowest_is1, n_gate_2_if_is_0, n_gate_2_if_lowest_is1, Time;
  wire [31:0] Counter;

  Clock clock_1 (.out(Time));
  Counter #(.width(32), .max('hffffffff)) counter_1 (.Q(Counter), .clk(Time));  // open: load, D, count, carry, clr
  n_gate n_gate_1 (.N(N), .if_lowest_is1(if_lowest_is1), .if_is_0(if_is_0));  // open: Counter
  n_gate n_gate_2 (.N(N), .Counter(Counter), .if_lowest_is1(n_gate_2_if_lowest_is1), .if_is_0(n_gate_2_if_is_0));
  mutex mutex_1 (
    .in_1(n_gate_2_if_lowest_is1), .in_2(n_gate_2_if_is_0), .in_3(Counter), .out_4(out_2), .out_5(out_3),
    .out_6(out_4), .out_7(out_5));

  // Other names for the same wires on the sheet: input_N[31:0] = N
endmodule

module n_gate (
  input  [31:0] N,
  input  [31:0] Counter,
  output if_lowest_is1,
  output if_is_0
);

  wire bitfinder_1_found, clock_1_out, comparator_1_eq, comparator_2_eq, not_2_out;
  wire [4:0] bitfinder_1_index;
  wire [31:0] left_move, multiplexer_1_out, register_1_q;

  // Probe on left_move
  Comparator #(.width(32)) comparator_1 (.a(Counter), .b({32{1'b0}}), .eq(comparator_1_eq));  // open: gt, lt
  // Probe on multiplexer_1_out
  Multiplexer #(.width(32)) multiplexer_1 (
    .in0(left_move), .in1(N), .out(multiplexer_1_out), .sel(comparator_1_eq));  // open: en
  Register #(.width(32)) register_1 (.D(multiplexer_1_out), .Q(register_1_q), .clk(clock_1_out));  // open: en, clr
  Clock clock_1 (.out(clock_1_out));
  BitFinder #(.width(32)) bitfinder_1 (.in(register_1_q), .index(bitfinder_1_index), .found(bitfinder_1_found));
  Comparator #(.width(5)) comparator_2 (.a(bitfinder_1_index), .b({5{1'b0}}), .eq(comparator_2_eq));  // open: gt, lt
  not not_1 (if_is_0, bitfinder_1_found);
  and and_1 (if_lowest_is1, comparator_2_eq, not_2_out);
  not not_2 (not_2_out, if_is_0);
  Shifter #(.width(32), .shift("lr")) shifter_1 (.in(register_1_q), .\dist (5'b00001), .out(left_move));
endmodule

module mutex (
  input  in_1,
  input  in_2,
  input  [31:0] in_3,
  output [31:0] out_4,
  output [31:0] out_5,
  output [31:0] out_6,
  output [31:0] out_7
);

  wire comparator_1_eq, comparator_2_eq, comparator_3_eq, comparator_4_eq, comparator_5_eq, comparator_6_eq,
       comparator_7_eq, comparator_8_eq, not_1_out, not_2_out, not_3_out, not_4_out, not_5_out, not_6_out,
       not_7_out, not_8_out, Time;
  wire [31:0] A11, A11_q, a11_t, A12, A12_q, a12_t, A21, A21_q, a21_t, A22, A22_q, a22_t, multiplexer_1_out,
       multiplexer_2_out, multiplexer_7_out, multiplexer_8_out, S11, S11_q, s11_t, S12, S12_q, s12_t, S21,
       S21_q, s21_t, S22, S22_q, s22_t;

  Clock clock_1 (.out(Time));
  Register #(.width(32)) u_S11 (.D(multiplexer_1_out), .Q(S11_q), .clk(Time));  // open: en, clr
  Multiplexer #(.width(32)) multiplexer_1 (.in0(S11), .in1(s11_t), .out(multiplexer_1_out), .sel(in_1));  // open: en
  Comparator #(.width(32)) comparator_1 (.a(in_3), .b({32{1'b0}}), .eq(comparator_1_eq));  // open: gt, lt
  Register #(.width(32)) u_S21 (.D(multiplexer_2_out), .Q(S21_q), .clk(Time));  // open: en, clr
  Multiplexer #(.width(32)) multiplexer_2 (.in0(S21), .in1(s21_t), .out(multiplexer_2_out), .sel(in_1));  // open: en
  Comparator #(.width(32)) comparator_2 (.a(in_3), .b({32{1'b0}}), .eq(comparator_2_eq));  // open: gt, lt
  Multiplexer #(.width(32)) multiplexer_3 (.in0(32'h1), .in1(S11_q), .out(S11), .sel(comparator_1_eq));  // open: en
  Multiplexer #(.width(32)) multiplexer_4 (.in0(32'h1), .in1(S21_q), .out(S21), .sel(comparator_2_eq));  // open: en
  Register #(.width(32)) u_A11 (.D(a11_t), .Q(A11_q), .clk(Time));  // open: en, clr
  not not_1 (not_1_out, comparator_3_eq);
  Comparator #(.width(32)) comparator_3 (.a(in_3), .b({32{1'b0}}), .eq(comparator_3_eq));  // open: gt, lt
  Register #(.width(32)) u_A21 (.D(a21_t), .Q(A21_q), .clk(Time));  // open: en, clr
  not not_2 (not_2_out, comparator_4_eq);
  Comparator #(.width(32)) comparator_4 (.a(in_3), .b({32{1'b0}}), .eq(comparator_4_eq));  // open: gt, lt
  Multiplexer #(.width(32)) multiplexer_5 (.in0(32'h1), .in1(A11_q), .out(A11), .sel(not_1_out));  // open: en
  Multiplexer #(.width(32)) multiplexer_6 (.in0(32'h1), .in1(A21_q), .out(A21), .sel(not_2_out));  // open: en
  Multiplexer #(.width(32)) multiplexer_7 (.in0(S12), .in1(s12_t), .out(multiplexer_7_out), .sel(in_1));  // open: en
  Multiplexer #(.width(32)) multiplexer_8 (.in0(S22), .in1(s22_t), .out(multiplexer_8_out), .sel(in_1));  // open: en
  Multiplexer #(.width(32)) multiplexer_9 (.in0(32'h1), .in1(S12_q), .out(S12), .sel(comparator_5_eq));  // open: en
  Register #(.width(32)) u_S12 (.D(multiplexer_7_out), .Q(S12_q), .clk(Time));  // open: en, clr
  Comparator #(.width(32)) comparator_5 (.a(in_3), .b({32{1'b0}}), .eq(comparator_5_eq));  // open: gt, lt
  Multiplexer #(.width(32)) multiplexer_10 (.in0(32'h1), .in1(S22_q), .out(S22), .sel(comparator_6_eq));  // open: en
  Register #(.width(32)) u_S22 (.D(multiplexer_8_out), .Q(S22_q), .clk(Time));  // open: en, clr
  Comparator #(.width(32)) comparator_6 (.a(in_3), .b({32{1'b0}}), .eq(comparator_6_eq));  // open: gt, lt
  Register #(.width(32)) u_A12 (.D(a12_t), .Q(A12_q), .clk(Time));  // open: en, clr
  not not_3 (not_3_out, comparator_7_eq);
  Comparator #(.width(32)) comparator_7 (.a(in_3), .b({32{1'b0}}), .eq(comparator_7_eq));  // open: gt, lt
  Register #(.width(32)) u_A22 (.D(a22_t), .Q(A22_q), .clk(Time));  // open: en, clr
  not not_4 (not_4_out, comparator_8_eq);
  Comparator #(.width(32)) comparator_8 (.a(in_3), .b({32{1'b0}}), .eq(comparator_8_eq));  // open: gt, lt
  Multiplexer #(.width(32)) multiplexer_11 (.in0(32'h1), .in1(A12_q), .out(A12), .sel(not_3_out));  // open: en
  Multiplexer #(.width(32)) multiplexer_12 (.in0(32'h1), .in1(A22_q), .out(A22), .sel(not_4_out));  // open: en
  Multiplexer #(.width(32)) multiplexer_13 (.in0(S11), .in1({32{1'b0}}), .out(out_4), .sel(not_5_out));  // open: en
  not not_5 (not_5_out, in_2);
  Multiplexer #(.width(32)) multiplexer_14 (.in0(S21), .in1({32{1'b0}}), .out(out_6), .sel(not_6_out));  // open: en
  not not_6 (not_6_out, in_2);
  mutex_square mutex_square_1 (
    .a11(A11), .a12(A12), .a21(A21), .a22(A22), .b11(a11_t), .b12(a12_t), .b21(a21_t), .b22(a22_t));
  mutex_mul mutex_mul_1 (
    .a11(A11), .b11(A12), .a12(A21), .b12(A22), .a21(S11), .b21(S12), .a22(S21), .b22(S22), .c11(s11_t),
    .c12(s11_t), .c21(s11_t), .c22(s11_t));
  Multiplexer #(.width(32)) multiplexer_15 (.in0(S12), .in1({32{1'b0}}), .out(out_5), .sel(not_7_out));  // open: en
  not not_7 (not_7_out, in_2);
  Multiplexer #(.width(32)) multiplexer_16 (.in0(S22), .in1({32{1'b0}}), .out(out_7), .sel(not_8_out));  // open: en
  not not_8 (not_8_out, in_2);

  // Other names for the same wires on the sheet: Counter[31:0] = in_3; if_is_0 = in_2; if_lowest_is1 = in_1
endmodule

module mutex_mul (
  input  [31:0] a11,
  input  [31:0] b11,
  input  [31:0] a12,
  input  [31:0] b12,
  input  [31:0] a21,
  input  [31:0] b21,
  input  [31:0] a22,
  input  [31:0] b22,
  output [31:0] c11,
  output [31:0] c12,
  output [31:0] c21,
  output [31:0] c22
);

  wire [31:0] multiplier_1_out, multiplier_2_out, multiplier_3_out, multiplier_4_out, multiplier_5_out,
       multiplier_6_out, multiplier_7_out, multiplier_8_out;

  Multiplier #(.width(32)) multiplier_1 (.a(a11), .b(b11), .out(multiplier_1_out));  // open: cin, cout
  Multiplier #(.width(32)) multiplier_2 (.a(a12), .b(b21), .out(multiplier_2_out));  // open: cin, cout
  Multiplier #(.width(32)) multiplier_3 (.a(a11), .b(b12), .out(multiplier_3_out));  // open: cin, cout
  Multiplier #(.width(32)) multiplier_4 (.a(a12), .b(b22), .out(multiplier_4_out));  // open: cin, cout
  Multiplier #(.width(32)) multiplier_5 (.a(a21), .b(b11), .out(multiplier_5_out));  // open: cin, cout
  Multiplier #(.width(32)) multiplier_6 (.a(a22), .b(b21), .out(multiplier_6_out));  // open: cin, cout
  Multiplier #(.width(32)) multiplier_7 (.a(a21), .b(b12), .out(multiplier_7_out));  // open: cin, cout
  Multiplier #(.width(32)) multiplier_8 (.a(a22), .b(b22), .out(multiplier_8_out));  // open: cin, cout
  Adder #(.width(32)) adder_1 (.a(multiplier_1_out), .b(multiplier_2_out), .out(c11));  // open: cin, cout
  Adder #(.width(32)) adder_2 (.a(multiplier_3_out), .b(multiplier_4_out), .out(c12));  // open: cin, cout
  Adder #(.width(32)) adder_3 (.a(multiplier_5_out), .b(multiplier_6_out), .out(c21));  // open: cin, cout
  Adder #(.width(32)) adder_4 (.a(multiplier_7_out), .b(multiplier_8_out), .out(c22));  // open: cin, cout
endmodule

module mutex_square (
  input  [31:0] a11,
  input  [31:0] a12,
  input  [31:0] a21,
  input  [31:0] a22,
  output [31:0] b11,
  output [31:0] b12,
  output [31:0] b21,
  output [31:0] b22
);

  wire [31:0] multiplier_1_out, multiplier_2_out, multiplier_3_out, multiplier_4_out, multiplier_5_out,
       multiplier_6_out, multiplier_7_out, multiplier_8_out;

  Multiplier #(.width(32)) multiplier_1 (.a(a11), .b(a11), .out(multiplier_1_out));  // open: cin, cout
  Multiplier #(.width(32)) multiplier_2 (.a(a12), .b(a21), .out(multiplier_2_out));  // open: cin, cout
  Multiplier #(.width(32)) multiplier_3 (.a(a11), .b(a12), .out(multiplier_3_out));  // open: cin, cout
  Multiplier #(.width(32)) multiplier_4 (.a(a12), .b(a22), .out(multiplier_4_out));  // open: cin, cout
  Multiplier #(.width(32)) multiplier_5 (.a(a11), .b(a21), .out(multiplier_5_out));  // open: cin, cout
  Multiplier #(.width(32)) multiplier_6 (.a(a21), .b(a22), .out(multiplier_6_out));  // open: cin, cout
  Multiplier #(.width(32)) multiplier_7 (.a(a12), .b(a21), .out(multiplier_7_out));  // open: cin, cout
  Multiplier #(.width(32)) multiplier_8 (.a(a22), .b(a22), .out(multiplier_8_out));  // open: cin, cout
  Adder #(.width(32)) adder_1 (.a(multiplier_1_out), .b(multiplier_2_out), .out(b11));  // open: cin, cout
  Adder #(.width(32)) adder_2 (.a(multiplier_3_out), .b(multiplier_4_out), .out(b12));  // open: cin, cout
  Adder #(.width(32)) adder_3 (.a(multiplier_5_out), .b(multiplier_6_out), .out(b21));  // open: cin, cout
  Adder #(.width(32)) adder_4 (.a(multiplier_7_out), .b(multiplier_8_out), .out(b22));  // open: cin, cout
endmodule
