// Logisim project 1109-23 fibonacci.circ as structural Verilog: 1 circuit, main circuit main
module main (
  input  [2:0] in_1,
  output [3:0] out_2
);

  wire clock_1_out, comparator_1_eq, comparator_2_eq, controlled_buffer_1_out, not_1_out;
  wire [3:0] adder_1_out, bit_extender_1_out, counter_1_q, multiplexer_1_out, register_1_q, register_2_q;

  // Probe on register_1_q
  Register #(.width(4)) register_1 (.D(adder_1_out), .Q(register_1_q), .clk(controlled_buffer_1_out));  // open: en, clr
  Counter #(.width(4), .max('hf)) counter_1 (
    .Q(counter_1_q), .clk(controlled_buffer_1_out));  // open: load, D, count, carry, clr
  assign bit_extender_1_out = {{1{1'b0}}, in_1};  // Bit_Extender bit_extender_1
  // Probe on multiplexer_1_out
  Multiplexer #(.width(4)) multiplexer_1 (
    .in0(register_1_q), .in1(4'b0001), .out(multiplexer_1_out), .sel(comparator_1_eq));  // open: en
  Comparator #(.width(4)) comparator_1 (.a(4'b0000), .b(counter_1_q), .eq(comparator_1_eq));  // open: gt, lt
  // Probe on comparator_1_eq
  assign controlled_buffer_1_out = not_1_out ? clock_1_out : 1'bz;  // Controlled_Buffer controlled_buffer_1
  Clock clock_1 (.out(clock_1_out));
  Comparator #(.width(4)) comparator_2 (.a(counter_1_q), .b(bit_extender_1_out), .eq(comparator_2_eq));  // open: gt, lt
  not not_1 (not_1_out, comparator_2_eq);
  // Probe on register_2_q
  Register #(.width(4)) register_2 (
    .D(multiplexer_1_out), .Q(register_2_q), .clk(controlled_buffer_1_out));  // open: en, clr
  Multiplexer #(.width(4)) multiplexer_2 (.in0(register_2_q), .in1(4'b0000), .out(out_2), .sel(not_1_out));  // open: en
  // Probe on adder_1_out
  Adder #(.width(4)) adder_1 (.a(multiplexer_1_out), .b(register_2_q), .out(adder_1_out));  // open: cin, cout
endmodule
