// Logisim project 1119-13 CRC-produce.circ as structural Verilog
module _4mod2 (
  input  [3:0] A,
  input  [3:0] B,
  output \商 ,
  output [3:0] \余数 
);

  wire comparator_1_eq;
  wire [3:0] multiplexer_2_out, shifter_1_out, xor_1_out, xor_2_out;

  Shifter #(.width(4), .shift("lr")) shifter_1 (.in(A), .\dist (2'b11), .out(shifter_1_out));
  assign xor_1_out = shifter_1_out ^ 4'b0001;  // XOR_Gate xor_1, 4 bits wide
  Comparator #(.width(4)) comparator_1 (.a(xor_1_out), .b(4'b0000), .eq(comparator_1_eq));  // open: gt, lt
  assign xor_2_out = A ^ B;  // XOR_Gate xor_2, 4 bits wide
  Multiplexer multiplexer_1 (.in0(1'b0), .in1(1'b1), .out(\商 ), .sel(comparator_1_eq), .en(1'b1));
  Multiplexer #(.width(4)) multiplexer_2 (.in0(A), .in1(xor_2_out), .out(multiplexer_2_out), .sel(\商 ), .en(1'b1));
  Shifter #(.width(4)) shifter_2 (.in(multiplexer_2_out), .\dist (2'b01), .out(\余数 ));
endmodule

module CRC (
  input  [7:0] A,
  input  [3:0] B,
  output [10:0] C
);

  wire bit_extender_6_out, bit_extender_7_out, bit_extender_9_out, bit_extender_11_out, bit_extender_14_out,
       bit_extender_15_out, bit_extender_17_out;
  wire [3:0] bit_extender_2_out, bit_extender_5_out, bit_extender_8_out, bit_extender_10_out,
       bit_extender_12_out, bit_extender_13_out, bit_extender_16_out, bit_extender_18_out, \n4mod2_1_余数 ,
       \n4mod2_2_余数 , \n4mod2_3_余数 , \n4mod2_4_余数 , \n4mod2_5_余数 , \n4mod2_6_余数 , \n4mod2_7_余数 , or_2_out,
       or_3_out, or_4_out, or_5_out, or_6_out, or_7_out, or_8_out, out, shifter_2_out;
  wire [10:0] bit_extender_1_out, bit_extender_3_out, bit_extender_4_out, divided, shifter_1_out,
       shifter_3_out, shifter_4_out, shifter_6_out, shifter_7_out, shifter_8_out, shifter_9_out,
       shifter_10_out, shifter_11_out;

  // Probe on out
  Shifter #(.width(11), .shift("lr")) shifter_1 (.in(divided), .\dist (4'b0111), .out(shifter_1_out));
  Shifter #(.width(4), .shift("lr")) shifter_2 (.in(out), .\dist (2'b01), .out(shifter_2_out));
  assign bit_extender_1_out = {{3{1'b0}}, A};  // Bit_Extender bit_extender_1
  Bit_Extender #(.in_width(11), .out_width(4)) bit_extender_2 (.in(shifter_1_out), .out(bit_extender_2_out));
  Shifter #(.width(11), .shift("lr")) shifter_3 (.in(divided), .\dist (4'b0110), .out(shifter_3_out));
  assign bit_extender_3_out = {{7{1'b0}}, shifter_2_out};  // Bit_Extender bit_extender_3
  Shifter #(.width(11)) shifter_4 (.in(bit_extender_1_out), .\dist (4'b0011), .out(shifter_4_out));
  assign bit_extender_4_out = {{3{1'b0}}, A};  // Bit_Extender bit_extender_4
  _4mod2 u_4mod2_1 (.A(bit_extender_2_out), .B(B), .\余数 (\n4mod2_1_余数 ));  // open: 商
  assign bit_extender_5_out = {{3{1'b0}}, bit_extender_6_out};  // Bit_Extender bit_extender_5
  Bit_Extender #(.in_width(11), .out_width(1)) bit_extender_6 (.in(shifter_3_out), .out(bit_extender_6_out));
  assign C = bit_extender_3_out | shifter_4_out;  // OR_Gate or_1, 11 bits wide
  Shifter #(.width(11)) shifter_5 (.in(bit_extender_4_out), .\dist (4'b0011), .out(divided));
  assign or_2_out = \n4mod2_1_余数  | bit_extender_5_out;  // OR_Gate or_2, 4 bits wide
  Shifter #(.width(11), .shift("lr")) shifter_6 (.in(divided), .\dist (4'b0101), .out(shifter_6_out));
  Bit_Extender #(.in_width(11), .out_width(1)) bit_extender_7 (.in(shifter_6_out), .out(bit_extender_7_out));
  _4mod2 u_4mod2_2 (.A(or_2_out), .B(B), .\余数 (\n4mod2_2_余数 ));  // open: 商
  assign bit_extender_8_out = {{3{1'b0}}, bit_extender_7_out};  // Bit_Extender bit_extender_8
  Shifter #(.width(11), .shift("lr")) shifter_7 (.in(divided), .\dist (4'b0100), .out(shifter_7_out));
  assign or_3_out = \n4mod2_2_余数  | bit_extender_8_out;  // OR_Gate or_3, 4 bits wide
  Bit_Extender #(.in_width(11), .out_width(1)) bit_extender_9 (.in(shifter_7_out), .out(bit_extender_9_out));
  _4mod2 u_4mod2_3 (.A(or_3_out), .B(B), .\余数 (\n4mod2_3_余数 ));  // open: 商
  assign or_4_out = \n4mod2_3_余数  | bit_extender_10_out;  // OR_Gate or_4, 4 bits wide
  assign bit_extender_10_out = {{3{1'b0}}, bit_extender_9_out};  // Bit_Extender bit_extender_10
  Shifter #(.width(11), .shift("lr")) shifter_8 (.in(divided), .\dist (4'b0011), .out(shifter_8_out));
  _4mod2 u_4mod2_4 (.A(or_4_out), .B(B), .\余数 (\n4mod2_4_余数 ));  // open: 商
  Bit_Extender #(.in_width(11), .out_width(1)) bit_extender_11 (.in(shifter_8_out), .out(bit_extender_11_out));
  assign bit_extender_12_out = {{3{1'b0}}, bit_extender_11_out};  // Bit_Extender bit_extender_12
  assign or_5_out = \n4mod2_4_余数  | bit_extender_12_out;  // OR_Gate or_5, 4 bits wide
  Shifter #(.width(11), .shift("lr")) shifter_9 (.in(divided), .\dist (4'b0010), .out(shifter_9_out));
  _4mod2 u_4mod2_5 (.A(or_5_out), .B(B), .\余数 (\n4mod2_5_余数 ));  // open: 商
  assign bit_extender_13_out = {{3{1'b0}}, bit_extender_14_out};  // Bit_Extender bit_extender_13
  Bit_Extender #(.in_width(11), .out_width(1)) bit_extender_14 (.in(shifter_9_out), .out(bit_extender_14_out));
  assign or_6_out = \n4mod2_5_余数  | bit_extender_13_out;  // OR_Gate or_6, 4 bits wide
  Shifter #(.width(11), .shift("lr")) shifter_10 (.in(divided), .\dist (4'b0001), .out(shifter_10_out));
  Bit_Extender #(.in_width(11), .out_width(1)) bit_extender_15 (.in(shifter_10_out), .out(bit_extender_15_out));
  _4mod2 u_4mod2_6 (.A(or_6_out), .B(B), .\余数 (\n4mod2_6_余数 ));  // open: 商
  assign bit_extender_16_out = {{3{1'b0}}, bit_extender_15_out};  // Bit_Extender bit_extender_16
  Shifter #(.width(11), .shift("lr")) shifter_11 (.in(divided), .\dist (4'b0000), .out(shifter_11_out));
  assign or_7_out = \n4mod2_6_余数  | bit_extender_16_out;  // OR_Gate or_7, 4 bits wide
  Bit_Extender #(.in_width(11), .out_width(1)) bit_extender_17 (.in(shifter_11_out), .out(bit_extender_17_out));
  _4mod2 u_4mod2_7 (.A(or_7_out), .B(B), .\余数 (\n4mod2_7_余数 ));  // open: 商
  assign or_8_out = \n4mod2_7_余数  | bit_extender_18_out;  // OR_Gate or_8, 4 bits wide
  assign bit_extender_18_out = {{3{1'b0}}, bit_extender_17_out};  // Bit_Extender bit_extender_18
  // Probe on out
  _4mod2 u_4mod2_8 (.A(or_8_out), .B(B), .\余数 (out));  // open: 商
endmodule
