// Logisim project 1119-269 GRF.circ as structural Verilog
module grf (
  input  clk,
  input  reset,
  input  WE,
  input  [4:0] A1,
  input  [4:0] A2,
  input  [4:0] A3,
  input  [31:0] WD,
  output [31:0] RD1,
  output [31:0] RD2
);

  wire WE0, WE1, WE2, WE3, WE4, WE5, WE6, WE7, WE8, WE9, WE10, WE11, WE12, WE13, WE14, WE15, WE16, WE17,
       WE18, WE19, WE20, WE21, WE22, WE23, WE24, WE25, WE26, WE27, WE28, WE29, WE30, WE31;
  wire [31:0] O1, O2, O3, O4, O5, O6, O7, O8, O9, O10, O11, O12, O13, O14, O15, O16, O17, O18, O19, O20, O21,
       O22, O23, O24, O25, O26, O27, O28, O29, O30, O31;

  Register #(.width(32)) R0 (.en(WE0), .clk(clk), .clr(reset));  // open: D, Q
  Register #(.width(32)) R8 (.D(WD), .en(WE8), .Q(O8), .clk(clk), .clr(reset));
  Register #(.width(32)) R16 (.D(WD), .en(WE16), .Q(O16), .clk(clk), .clr(reset));
  Register #(.width(32)) R24 (.D(WD), .en(WE24), .Q(O24), .clk(clk), .clr(reset));
  Multiplexer #(.select(5), .width(32)) multiplexer_1 (
    .in0({32{1'b0}}), .in1(O1), .in2(O2), .in3(O3), .in4(O4), .in5(O5), .in6(O6), .in7(O7), .in8(O8),
    .in9(O9), .in10(O10), .in11(O11), .in12(O12), .in13(O13), .in14(O14), .in15(O15), .in16(O16), .in17(O17),
    .in18(O18), .in19(O19), .in20(O20), .in21(O21), .in22(O22), .in23(O23), .in24(O24), .in25(O25),
    .in26(O26), .in27(O27), .in28(O28), .in29(O29), .in30(O30), .in31(O31), .out(RD1), .sel(A1), .en(1'b1));
  Register #(.width(32)) R1 (.D(WD), .en(WE1), .Q(O1), .clk(clk), .clr(reset));
  Register #(.width(32)) R9 (.D(WD), .en(WE9), .Q(O9), .clk(clk), .clr(reset));
  Register #(.width(32)) R17 (.D(WD), .en(WE17), .Q(O17), .clk(clk), .clr(reset));
  Register #(.width(32)) R25 (.D(WD), .en(WE25), .Q(O25), .clk(clk), .clr(reset));
  Register #(.width(32)) R2 (.D(WD), .en(WE2), .Q(O2), .clk(clk), .clr(reset));
  Register #(.width(32)) R10 (.D(WD), .en(WE10), .Q(O10), .clk(clk), .clr(reset));
  Register #(.width(32)) R18 (.D(WD), .en(WE18), .Q(O18), .clk(clk), .clr(reset));
  Register #(.width(32)) R26 (.D(WD), .en(WE26), .Q(O26), .clk(clk), .clr(reset));
  Multiplexer #(.select(5), .width(32)) multiplexer_2 (
    .in0({32{1'b0}}), .in1(O1), .in2(O2), .in3(O3), .in4(O4), .in5(O5), .in6(O6), .in7(O7), .in8(O8),
    .in9(O9), .in10(O10), .in11(O11), .in12(O12), .in13(O13), .in14(O14), .in15(O15), .in16(O16), .in17(O17),
    .in18(O18), .in19(O19), .in20(O20), .in21(O21), .in22(O22), .in23(O23), .in24(O24), .in25(O25),
    .in26(O26), .in27(O27), .in28(O28), .in29(O29), .in30(O30), .in31(O31), .out(RD2), .sel(A2), .en(1'b1));
  Register #(.width(32)) R3 (.D(WD), .en(WE3), .Q(O3), .clk(clk), .clr(reset));
  Register #(.width(32)) R11 (.D(WD), .en(WE11), .Q(O11), .clk(clk), .clr(reset));
  Register #(.width(32)) R19 (.D(WD), .en(WE19), .Q(O19), .clk(clk), .clr(reset));
  Register #(.width(32)) R27 (.D(WD), .en(WE27), .Q(O27), .clk(clk), .clr(reset));
  Demultiplexer #(.select(5)) demultiplexer_1 (
    .out0(WE0), .out1(WE1), .out2(WE2), .out3(WE3), .out4(WE4), .out5(WE5), .out6(WE6), .out7(WE7),
    .out8(WE8), .out9(WE9), .out10(WE10), .out11(WE11), .out12(WE12), .out13(WE13), .out14(WE14),
    .out15(WE15), .out16(WE16), .out17(WE17), .out18(WE18), .out19(WE19), .out20(WE20), .out21(WE21),
    .out22(WE22), .out23(WE23), .out24(WE24), .out25(WE25), .out26(WE26), .out27(WE27), .out28(WE28),
    .out29(WE29), .out30(WE30), .out31(WE31), .in(WE), .sel(A3), .en(1'b1));
  Register #(.width(32)) R4 (.D(WD), .en(WE4), .Q(O4), .clk(clk), .clr(reset));
  Register #(.width(32)) R12 (.D(WD), .en(WE12), .Q(O12), .clk(clk), .clr(reset));
  Register #(.width(32)) R20 (.D(WD), .en(WE20), .Q(O20), .clk(clk), .clr(reset));
  Register #(.width(32)) R28 (.D(WD), .en(WE28), .Q(O28), .clk(clk), .clr(reset));
  Register #(.width(32)) R5 (.D(WD), .en(WE5), .Q(O5), .clk(clk), .clr(reset));
  Register #(.width(32)) R13 (.D(WD), .en(WE13), .Q(O13), .clk(clk), .clr(reset));
  Register #(.width(32)) R21 (.D(WD), .en(WE21), .Q(O21), .clk(clk), .clr(reset));
  Register #(.width(32)) R29 (.D(WD), .en(WE29), .Q(O29), .clk(clk), .clr(reset));
  Register #(.width(32)) R6 (.D(WD), .en(WE6), .Q(O6), .clk(clk), .clr(reset));
  Register #(.width(32)) R14 (.D(WD), .en(WE14), .Q(O14), .clk(clk), .clr(reset));
  Register #(.width(32)) R22 (.D(WD), .en(WE22), .Q(O22), .clk(clk), .clr(reset));
  Register #(.width(32)) R30 (.D(WD), .en(WE30), .Q(O30), .clk(clk), .clr(reset));
  Register #(.width(32)) R7 (.D(WD), .en(WE7), .Q(O7), .clk(clk), .clr(reset));
  Register #(.width(32)) R15 (.D(WD), .en(WE15), .Q(O15), .clk(clk), .clr(reset));
  Register #(.width(32)) R23 (.D(WD), .en(WE23), .Q(O23), .clk(clk), .clr(reset));
  Register #(.width(32)) R31 (.D(WD), .en(WE31), .Q(O31), .clk(clk), .clr(reset));
endmodule
