// Logisim project 1119-319 ftoi.circ as structural Verilog
module ftoi (
  input  [15:0] float,
  output [31:0] \int 
);

  wire _0, comparator_1_eq, comparator_3_eq, or_1_out, s;
  wire [2:0] comparator_2_gt;
  wire [4:0] e, exp, subtractor_1_out, subtractor_2_out;
  wire [9:0] frac;
  wire [31:0] adder_1_out, bit_extender_1_out, exp_10, exp_10_t, multiplexer_1_out, not_1_out, num, or_2_out,
       \拼接后的frac ;

  Subtractor #(.width(5)) subtractor_1 (.a(5'b01010), .b(exp), .out(subtractor_1_out));  // open: bin, bout
  Subtractor #(.width(5)) subtractor_2 (.a(exp), .b(5'b01010), .out(subtractor_2_out));  // open: bin, bout
  assign not_1_out = ~num;  // NOT_Gate not_1, 32 bits wide
  separate separate (.ori(float), .s(s), .exponent(e), .fraction(frac));
  Shifter #(.width(32), .shift("lr")) shifter_1 (.in(\拼接后的frac ), .\dist (subtractor_1_out), .out(exp_10));
  Shifter #(.width(32)) shifter_2 (.in(\拼接后的frac ), .\dist (subtractor_2_out), .out(exp_10_t));
  Adder #(.width(32)) adder_1 (.a(not_1_out), .b(32'h1), .out(adder_1_out));  // open: cin, cout
  Multiplexer #(.width(32)) multiplexer_1 (.in0(num), .in1(adder_1_out), .out(multiplexer_1_out), .sel(s), .en(1'b1));
  Comparator #(.width(5)) comparator_1 (.a(e), .b({5{1'b1}}), .eq(comparator_1_eq));  // open: gt, lt
  Subtractor #(.width(5)) subtractor_3 (.a(e), .b(5'b01111), .out(exp), .bout(_0));  // open: bin
  Multiplexer #(.width(32)) multiplexer_2 (
    .in0(multiplexer_1_out), .in1({32{1'b0}}), .out(\int ), .sel(or_1_out), .en(1'b1));
  or or_1 (or_1_out, comparator_1_eq, _0);
  Comparator #(.width(5)) comparator_2 (
    .a(exp), .b(5'b01010), .gt(comparator_2_gt[0]), .eq(comparator_2_gt[1]), .lt(comparator_2_gt[2]));
  Multiplexer #(.select(3), .width(32)) multiplexer_3 (
    .in1(exp_10_t), .in2(\拼接后的frac ), .in4(exp_10), .out(num), .sel(comparator_2_gt), .en(1'b1));  // open: in0, in3, in5, in6, in7
  assign or_2_out = 32'h400 | bit_extender_1_out;  // OR_Gate or_2, 32 bits wide
  assign bit_extender_1_out = {{22{1'b0}}, frac};  // Bit_Extender bit_extender_1
  Comparator #(.width(5)) comparator_3 (.a(e), .b({5{1'b0}}), .eq(comparator_3_eq));  // open: gt, lt
  Multiplexer #(.width(32)) multiplexer_4 (
    .in0(or_2_out), .in1(bit_extender_1_out), .out(\拼接后的frac ), .sel(comparator_3_eq), .en(1'b1));
endmodule

module separate (
  input  [15:0] ori,
  output s,
  output [4:0] exponent,
  output [9:0] fraction
);

  wire [15:0] shifter_1_out, shifter_2_out;

  Bit_Extender #(.in_width(16), .out_width(1)) bit_extender_1 (.in(shifter_1_out), .out(s));
  Shifter #(.width(16), .shift("lr")) shifter_1 (.in(ori), .\dist (4'b1111), .out(shifter_1_out));
  Bit_Extender #(.in_width(16), .out_width(5)) bit_extender_2 (.in(shifter_2_out), .out(exponent));
  Shifter #(.width(16), .shift("lr")) shifter_2 (.in(ori), .\dist (4'b1010), .out(shifter_2_out));
  Bit_Extender #(.in_width(16), .out_width(10)) bit_extender_3 (.in(ori), .out(fraction));
endmodule
