// Logisim project 1119-393 navigation.circ as structural Verilog
module moore (
  input  [3:0] status,
  input  [1:0] \input ,
  output [3:0] next_status
);

  wire and_1_out, and_2_out, and_3_out, and_4_out, and_5_out, and_6_out, and_7_out, and_8_out, and_9_out,
       and_10_out, and_11_out, and_12_out, and_13_out, and_14_out, and_15_out, and_16_out, not_1_out,
       not_2_out, not_3_out, not_4_out, not_5_out, not_6_out, not_7_out, not_8_out, not_9_out, not_10_out,
       not_11_out, not_12_out, not_13_out, not_14_out, not_15_out, not_16_out, not_17_out, not_18_out,
       not_19_out, not_20_out, not_21_out, not_22_out, not_23_out, not_24_out, not_25_out, not_26_out,
       not_27_out, not_28_out;

  not not_1 (not_1_out, status[0]);
  not not_2 (not_2_out, \input [1]);
  not not_3 (not_3_out, \input [0]);
  not not_4 (not_4_out, \input [1]);
  not not_5 (not_5_out, status[0]);
  not not_6 (not_6_out, \input [1]);
  not not_7 (not_7_out, status[0]);
  not not_8 (not_8_out, \input [0]);
  not not_9 (not_9_out, status[2]);
  not not_10 (not_10_out, status[1]);
  not not_11 (not_11_out, \input [1]);
  not not_12 (not_12_out, \input [0]);
  not not_13 (not_13_out, status[2]);
  not not_14 (not_14_out, status[0]);
  not not_15 (not_15_out, \input [1]);
  not not_16 (not_16_out, status[2]);
  not not_17 (not_17_out, status[1]);
  not not_18 (not_18_out, status[0]);
  not not_19 (not_19_out, status[2]);
  not not_20 (not_20_out, status[0]);
  not not_21 (not_21_out, \input [0]);
  not not_22 (not_22_out, \input [1]);
  not not_23 (not_23_out, \input [0]);
  and and_1 (and_1_out, status[1], not_1_out, not_2_out, not_3_out);
  and and_2 (and_2_out, status[1], status[0], not_4_out, \input [0]);
  not not_24 (not_24_out, status[1]);
  and and_3 (and_3_out, not_24_out, status[0], not_25_out);
  not not_25 (not_25_out, \input [1]);
  not not_26 (not_26_out, \input [1]);
  and and_4 (and_4_out, status[0], not_26_out, not_27_out);
  not not_27 (not_27_out, \input [0]);
  and and_5 (and_5_out, status[1], not_5_out, not_6_out, \input [0]);
  and and_6 (and_6_out, status[1], not_7_out, \input [1], not_8_out);
  and and_7 (and_7_out, status[1], status[0], \input [1], \input [0]);
  and and_8 (and_8_out, not_9_out, not_10_out, not_11_out, not_12_out);
  and and_9 (and_9_out, status[0], \input [1], \input [0]);
  and and_10 (and_10_out, status[1], \input [1], \input [0]);
  and and_11 (and_11_out, status[1], status[0], not_28_out);
  not not_28 (not_28_out, \input [0]);
  and and_12 (and_12_out, not_13_out, not_14_out, not_15_out, \input [0]);
  and and_13 (and_13_out, not_16_out, not_17_out, not_18_out, \input [1]);
  and and_14 (and_14_out, not_19_out, not_20_out, \input [1], not_21_out);
  and and_15 (and_15_out, status[0], \input [1], \input [0]);
  and and_16 (and_16_out, status[1], status[0], not_22_out, not_23_out);
  or or_1 (next_status[2], and_1_out, and_2_out);
  or or_2 (next_status[1], and_3_out, and_4_out, and_5_out, and_6_out, and_7_out);
  or or_3 (next_status[0], and_8_out, and_9_out, and_10_out, and_11_out);
  or or_4 (next_status[3], and_12_out, and_13_out, and_14_out, and_15_out, and_16_out);

  // Other names for the same wires on the sheet: N0 = \input [0]; N1 = \input [1]; S0 = next_status[0];
  //   S1 = next_status[1]; S2 = next_status[2]; hit = next_status[3]; I0 = status[0]; I1 = status[1]; I2 = status[2]
endmodule

module navigation (
  input  [1:0] dir,
  input  clk,
  input  reset,
  output arrive,
  output hit
);

  wire [3:0] and_1_out, moore_next_status, not_1_out, register_1_q, shifter_1_out;

  // Probe on moore_next_status
  moore moore (.status(register_1_q), .\input (dir), .next_status(moore_next_status));
  // Probe on register_1_q
  Register #(.width(4)) register_1 (.D(moore_next_status), .Q(register_1_q), .clk(clk), .clr(reset));  // open: en
  assign not_1_out = ~4'b1000;  // NOT_Gate not_1, 4 bits wide
  assign and_1_out = not_1_out & register_1_q;  // AND_Gate and_1, 4 bits wide
  Comparator #(.width(4)) comparator_1 (.a(and_1_out), .b(4'b0100), .eq(arrive));  // open: gt, lt
  Shifter #(.width(4), .shift("lr")) shifter_1 (.in(register_1_q), .\dist (2'b11), .out(shifter_1_out));
  Comparator #(.width(4)) comparator_2 (.a(shifter_1_out), .b(4'b0001), .eq(hit));  // open: gt, lt
endmodule
