// Logisim project 1119-9 FSM.circ as structural Verilog
module melay (
  input  [2:0] status,
  input  [1:0] \input ,
  output [2:0] next_status,
  output \output 
);

  wire and_2_out, and_3_out, and_4_out, and_5_out, and_6_out, and_7_out, and_8_out, and_9_out, not_1_out,
       not_2_out, not_3_out, not_4_out, not_5_out, not_6_out, not_7_out, not_8_out, not_9_out, not_10_out,
       not_11_out, not_12_out, not_13_out, not_14_out, not_15_out, not_16_out, not_17_out, not_18_out;

  not not_1 (not_1_out, \input [0]);
  not not_2 (not_2_out, status[1]);
  not not_3 (not_3_out, \input [1]);
  not not_4 (not_4_out, status[1]);
  not not_5 (not_5_out, \input [0]);
  not not_6 (not_6_out, status[0]);
  not not_7 (not_7_out, \input [1]);
  not not_8 (not_8_out, status[0]);
  not not_9 (not_9_out, \input [0]);
  not not_10 (not_10_out, status[1]);
  not not_11 (not_11_out, status[0]);
  not not_12 (not_12_out, \input [1]);
  not not_13 (not_13_out, \input [1]);
  not not_14 (not_14_out, \input [0]);
  and and_1 (next_status[2], status[1], status[0], not_1_out);
  and and_2 (and_2_out, not_2_out, status[0], not_3_out);
  and and_3 (and_3_out, not_4_out, status[0], not_5_out);
  and and_4 (and_4_out, status[1], not_6_out, not_7_out);
  and and_5 (and_5_out, status[1], not_8_out, not_9_out);
  and and_6 (and_6_out, not_10_out, not_11_out, not_12_out, \input [0]);
  not not_15 (not_15_out, status[1]);
  and and_7 (and_7_out, not_15_out, status[0], not_16_out);
  not not_16 (not_16_out, \input [0]);
  and and_8 (and_8_out, status[1], not_17_out, not_18_out);
  not not_17 (not_17_out, status[0]);
  not not_18 (not_18_out, \input [0]);
  and and_9 (and_9_out, status[1], status[0], not_13_out, \input [0]);
  and and_10 (\output , status[1], status[0], not_14_out);
  or or_1 (next_status[1], and_2_out, and_3_out, and_4_out, and_5_out);
  or or_2 (next_status[0], and_6_out, and_7_out, and_8_out, and_9_out);

  // Other names for the same wires on the sheet: I0 = \input [0]; I1 = \input [1]; S0 = next_status[0];
  //   S1 = next_status[1]; S2 = next_status[2]; out = \output ; O0 = status[0]; O1 = status[1]; O2 = status[2]
endmodule

module fsm (
  input  CLR,
  input  [1:0] In,
  output Z
);

  wire clock_1_out;
  wire [2:0] melay_next_status, multiplexer_1_out, register_1_q;

  Register #(.width(3)) register_1 (.D(multiplexer_1_out), .Q(register_1_q), .clk(clock_1_out));  // open: en, clr
  Multiplexer #(.width(3)) multiplexer_1 (
    .in0(melay_next_status), .in1(3'b000), .out(multiplexer_1_out), .sel(CLR), .en(1'b1));
  Clock clock_1 (.out(clock_1_out));
  melay melay (.status(register_1_q), .\input (In), .next_status(melay_next_status), .\output (Z));

  // Other names for the same wires on the sheet: input[1:0] = In
endmodule
