// Logisim project 4bit_sort.circ as structural Verilog
module _1bit_swap (
  input  i1,
  input  i2,
  input  s,
  output o1,
  output o2
);

  wire and_1_out, and_2_out, not_1_out, not_2_out, or_1_out, or_2_out;

  not not_1 (not_1_out, s);
  not not_2 (not_2_out, s);
  and and_1 (and_1_out, i2, s);
  and and_2 (and_2_out, i1, not_1_out);
  or or_1 (or_1_out, i2, s);
  or or_2 (or_2_out, i1, not_2_out);
  or or_3 (o1, and_1_out, and_2_out);
  and and_3 (o2, or_1_out, or_2_out);
endmodule

module _4bit_swap (
  input  [3:0] i1,
  input  [3:0] i2,
  input  in_3,
  output [3:0] _01,
  output [3:0] o2
);

  _1bit_swap u_1bit_swap_1 (.i1(i1[0]), .i2(i2[0]), .s(in_3), .o1(_01[0]), .o2(o2[0]));
  _1bit_swap u_1bit_swap_2 (.i1(i1[1]), .i2(i2[1]), .s(in_3), .o1(_01[1]), .o2(o2[1]));
  _1bit_swap u_1bit_swap_3 (.i1(i1[2]), .i2(i2[2]), .s(in_3), .o1(_01[2]), .o2(o2[2]));
  _1bit_swap u_1bit_swap_4 (.i1(i1[3]), .i2(i2[3]), .s(in_3), .o1(_01[3]), .o2(o2[3]));

  // Other names for the same wires on the sheet: flag = in_3
endmodule

module _4bit_sort (
  input  [3:0] A,
  input  [3:0] B,
  input  [3:0] C,
  input  [3:0] D,
  output [3:0] _1,
  output [3:0] _2,
  output [3:0] _3,
  output [3:0] _4
);

  wire [3:0] small_swap_1_output1, small_swap_1_output2, small_swap_2_output1, small_swap_2_output2,
       small_swap_3_output2, small_swap_5_output1;

  small_swap small_swap_1 (.input1(A), .input2(B), .output1(small_swap_1_output1), .output2(small_swap_1_output2));
  small_swap small_swap_2 (.input1(C), .input2(D), .output1(small_swap_2_output1), .output2(small_swap_2_output2));
  small_swap small_swap_3 (
    .input1(small_swap_1_output1), .input2(small_swap_2_output1), .output1(_1), .output2(small_swap_3_output2));
  small_swap small_swap_4 (.input1(small_swap_3_output2), .input2(small_swap_5_output1), .output1(_2), .output2(_3));
  small_swap small_swap_5 (
    .input1(small_swap_1_output2), .input2(small_swap_2_output2), .output1(small_swap_5_output1), .output2(_4));
endmodule

module small_swap (
  input  [3:0] input1,
  input  [3:0] input2,
  output [3:0] output1,
  output [3:0] output2
);

  wire comparator_1_gt;

  Comparator #(.width(4), .mode("unsigned")) comparator_1 (
    .a(input1), .b(input2), .gt(comparator_1_gt));  // open: eq, lt
  _4bit_swap u_4bit_swap_1 (.i1(input1), .i2(input2), .in_3(comparator_1_gt), ._01(output1), .o2(output2));
endmodule
