// Logisim project Logisim_swap.circ as structural Verilog
module swap (
  input  I1,
  input  I2,
  input  S,
  output O1,
  output O2
);

  wire and_1_out, and_2_out, and_3_out, and_4_out, controlled_buffer_1_out, controlled_buffer_2_out,
       not_1_out, not_2_out;

  and and_1 (and_1_out, I1, not_1_out);
  not not_1 (not_1_out, S);
  assign controlled_buffer_1_out = S ? I1 : 1'bz;  // Controlled_Buffer controlled_buffer_1
  assign controlled_buffer_2_out = S ? I2 : 1'bz;  // Controlled_Buffer controlled_buffer_2
  not not_2 (not_2_out, S);
  and and_2 (and_2_out, not_2_out, I2);
  and and_3 (and_3_out, controlled_buffer_1_out, S);
  and and_4 (and_4_out, controlled_buffer_2_out, S);
  or or_1 (O1, and_1_out, and_4_out);
  or or_2 (O2, and_3_out, and_2_out);
endmodule
